# Fritzing sketch schematic (saved by Fritzing 0.8.0b)
breadboards: 1

parts:
  R1 = Resistor [tolerance=±5% resistance=1k package=THT]
  R2 = Resistor [tolerance=±5% resistance=1k package=THT]
  R3 = Resistor [tolerance=±5% resistance=1k package=THT]
  R4 = Resistor [tolerance=±5% resistance=1k package=THT]
  U1 = 74HC595 [package="DIP16 [THT]"]
  Part1 = Arduino Uno (Rev3)

nets:
  N1: R1.Pin_0, U1.Q7
  N2: R1.Pin_1, U1.Q0
  N3: R2.Pin_0, U1.Q6
  N4: R2.Pin_1, U1.Q1
  N5: R3.Pin_0, U1.Q5
  N6: R3.Pin_1, U1.Q2
  N7: R4.Pin_0, U1.Q4
  N8: R4.Pin_1, U1.Q3
  GND: U1.GND, U1.OE, Part1.GND
  VCC: U1.MR, U1.VCC, Part1.5V
  N9: U1.SH_CP, Part1.D12/MISO
  N10: U1.ST_CP, Part1.D8
  N11: U1.DS, Part1.D11_PWM/MOSI

notes:
  Using a BL-M07C881UR 8x8 LED Matrix.
  Assuming that pin 1 is the leftpost pin, on the side where there is writing, plug these four resistors into leftmost pins on the side where there is no writing. The bottom 4 wires correspond with the four leftmost pins on the side where there is writing. If confused, look at picture. Ignore the direct wiring going through this note.
