# Fritzing sketch schematic (saved by Fritzing 0.8.0b)

parts:
  Microcontroller = Arduino Uno (Rev3)
  Column_Shift_Register = 74HC595 [package="DIP16 [THT]"]
  Row_Shift_Register = 74HC595 [package="DIP16 [THT]"]
  R1 = Resistor [tolerance=±5% resistance=1k package=THT]
  R2 = Resistor [tolerance=±5% resistance=1k package=THT]
  R3 = Resistor [tolerance=±5% resistance=1k package=THT]
  R4 = Resistor [tolerance=±5% resistance=1k package=THT]
  R5 = Resistor [tolerance=±5% resistance=1k package=THT]
  R6 = Resistor [tolerance=±5% resistance=1k package=THT]
  R7 = Resistor [tolerance=±5% resistance=1k package=THT]
  R8 = Resistor [tolerance=±5% resistance=1k package=THT]

nets:
  GND: Microcontroller.GND, Column_Shift_Register.GND, Column_Shift_Register.OE, Row_Shift_Register.GND, Row_Shift_Register.OE
  VCC: Microcontroller.5V, Column_Shift_Register.MR, Column_Shift_Register.VCC, Row_Shift_Register.MR, Row_Shift_Register.VCC
  N1: Microcontroller.D2, Row_Shift_Register.DS
  N2: Microcontroller.D3_PWM, Row_Shift_Register.SH_CP
  N3: Microcontroller.D4, Row_Shift_Register.ST_CP
  N4: Microcontroller.D5_PWM, Column_Shift_Register.DS
  N5: Microcontroller.D6_PWM, Column_Shift_Register.SH_CP
  N6: Microcontroller.D7, Column_Shift_Register.ST_CP
  N7: Column_Shift_Register.Q1, R2.Pin_1
  N8: Column_Shift_Register.Q2, R3.Pin_1
  N9: Column_Shift_Register.Q3, R4.Pin_1
  N10: Column_Shift_Register.Q4, R5.Pin_0
  N11: Column_Shift_Register.Q5, R6.Pin_0
  N12: Column_Shift_Register.Q6, R7.Pin_0
  N13: Column_Shift_Register.Q7, R8.Pin_0
  N14: Column_Shift_Register.Q0, R1.Pin_1
  N15: Row_Shift_Register.Q1, R3.Pin_0
  N16: Row_Shift_Register.Q2, R2.Pin_0
  N17: Row_Shift_Register.Q3, R1.Pin_0
  N18: Row_Shift_Register.Q4, R8.Pin_1
  N19: Row_Shift_Register.Q5, R7.Pin_1
  N20: Row_Shift_Register.Q6, R6.Pin_1
  N21: Row_Shift_Register.Q7, R5.Pin_1
  N22: Row_Shift_Register.Q0, R4.Pin_0

notes:
  <- Data (D2)
  <- Clock (D3)
  <- Latch (D4)
  Assume this block here is the BL-M07C881UR 8x8 LED Matrix. Pin 1 should be the lower left hand corner. The "Front portion is then the bottom of this block. There are 8 pins at the top, and 8 at the bottom.
